// Logisim project microprocessor.circ as structural Verilog: 4 circuits, main circuit CPU
module CPU (
);

  wire Clock, Program_Counter_carry, undriven, undriven_2, undriven_3, undriven_5, undriven_6, undriven_7,
       undriven_8, undriven_9, undriven_10, undriven_11, undriven_12, undriven_13, undriven_14, undriven_15,
       undriven_16, undriven_17, undriven_18, undriven_19;
  wire [2:0] ALU_Sel;
  wire [3:0] ADDR, adress_q, fsm_1_opcode, multiplexer_1_out, Program_Counter_q, undriven_4;
  wire [7:0] accumulator_1_output, aritmaticlogicunit_1_output, Input1, ram_1_data;
  wire [15:0] inst, rom_1_data;

  Clock clock_1 (.out(Clock));
  Counter #(.width(4), .max('h8)) Program_Counter (
    .D(adress_q), .count(undriven), .Q(Program_Counter_q), .carry(Program_Counter_carry), .clk(undriven_2),
    .clr(undriven_3));  // open: load
  Multiplexer #(.width(4), .enable("false")) multiplexer_1 (
    .in0(Program_Counter_q), .in1(ADDR), .out(multiplexer_1_out), .sel(undriven_6));
  Register #(.width(4)) adress (
    .D(multiplexer_1_out), .en(undriven_8), .Q(adress_q), .clk(undriven_10), .clr(undriven_12));
  RAM #(.addrWidth(4), .bus("separate")) ram_1 (
    .addr(undriven_4), .data(ram_1_data), .str(undriven_5), .sel(undriven_7), .ld(undriven_9),
    .clr(undriven_11));  // open: din, clk
  ROM #(.addrWidth(4), .dataWidth(16)) rom_1 (.addr(adress_q), .data(rom_1_data));  // open: sel
  Register #(.width(16)) Instruction_Register (
    .D(rom_1_data), .en(undriven_13), .Q(inst), .clk(undriven_14), .clr(undriven_15));
  AritmaticLogicUnit aritmaticlogicunit_1 (
    .ALU_Sel(ALU_Sel), .Output(aritmaticlogicunit_1_output), .Input2(accumulator_1_output), .Input1(Input1),
    .carryoutadd(undriven_16), .carryoutsub(undriven_17));
  FSM fsm_1 (.Instruction(inst), .ALU_SEL(ALU_Sel), .OPCODE(fsm_1_opcode), .ADDR(ADDR), .Input_1(Input1));
  Accumulator accumulator_1 (
    .Clock(Clock), .WE(undriven_18), .AscSet0(undriven_19), .Input(aritmaticlogicunit_1_output),
    .\output (accumulator_1_output));
endmodule

// ALU
module AritmaticLogicUnit (
  input  [7:0] Input1,
  input  [7:0] Input2,
  input  [2:0] ALU_Sel,
  input  carryoutadd,
  input  carryoutsub,
  output [7:0] Output
);

  wire [7:0] adda, anda, ora, shiftL, shiftR, suba;

  Adder adder_1 (.a(Input1), .b(Input2), .out(adda), .cin(1'b0), .cout(carryoutadd));
  Subtractor subtractor_1 (.a(Input1), .b(Input2), .out(suba), .bin(1'b0), .bout(carryoutsub));
  assign anda = Input1 & Input2;  // AND_Gate anda, 8 bits wide
  assign ora = Input1 | Input2;  // OR_Gate ora, 8 bits wide
  Shifter shifter_1 (.in(Input1), .\dist (3'b001), .out(shiftL));
  Shifter #(.shift("lr")) shifter_2 (.in(Input1), .\dist (3'b001), .out(shiftR));
  Multiplexer #(.select(3), .width(8), .enable("false")) multiplexer_1 (
    .in0(adda), .in1(suba), .in2(anda), .in3(ora), .in4(Input1), .in5(shiftL), .in6(shiftR), .in7({8{1'b0}}),
    .out(Output), .sel(ALU_Sel));

  // Other names for the same wires on the sheet: mova[7:0] = Input1
endmodule

module Accumulator (
  input  [7:0] Input,
  input  Clock,
  input  WE,
  input  AscSet0,
  output [7:0] \output 
);

  Pull_Resistor pull_resistor_1 (.node(AscSet0));
  D_Flip_Flop d_ff_1 (.clk(Clock), .D(Input[7]), .Q(\output [7]), .en(WE), .reset(AscSet0));  // open: Qn, preset
  D_Flip_Flop d_ff_2 (.clk(Clock), .D(Input[6]), .Q(\output [6]), .en(WE), .reset(AscSet0));  // open: Qn, preset
  D_Flip_Flop d_ff_3 (.clk(Clock), .D(Input[5]), .Q(\output [5]), .en(WE), .reset(AscSet0));  // open: Qn, preset
  D_Flip_Flop d_ff_4 (.clk(Clock), .D(Input[4]), .Q(\output [4]), .en(WE), .reset(AscSet0));  // open: Qn, preset
  D_Flip_Flop d_ff_5 (.clk(Clock), .D(Input[3]), .Q(\output [3]), .en(WE), .reset(AscSet0));  // open: Qn, preset
  D_Flip_Flop d_ff_6 (.clk(Clock), .D(Input[2]), .Q(\output [2]), .en(WE), .reset(AscSet0));  // open: Qn, preset
  D_Flip_Flop d_ff_7 (.clk(Clock), .D(Input[1]), .Q(\output [1]), .en(WE), .reset(AscSet0));  // open: Qn, preset
  D_Flip_Flop d_ff_8 (.clk(Clock), .D(Input[0]), .Q(\output [0]), .en(WE), .reset(AscSet0));  // open: Qn, preset

  // Other names for the same wires on the sheet: in0 = Input[0]; in1 = Input[1]; in2 = Input[2]; in3 = Input[3];
  //   in4 = Input[4]; in5 = Input[5]; in6 = Input[6]; in7 = Input[7]; out0 = \output [0]; out1 = \output [1];
  //   out2 = \output [2]; out3 = \output [3]; out4 = \output [4]; out5 = \output [5]; out6 = \output [6];
  //   out7 = \output [7]
endmodule

module FSM (
  input  [15:0] Instruction,
  output [2:0] ALU_SEL,
  output [3:0] OPCODE,
  output [3:0] ADDR,
  output [7:0] Input_1
);


  assign ADDR = Instruction[7:4];
  assign ALU_SEL = Instruction[2:0];
  assign Input_1 = {Instruction[8], Instruction[9], Instruction[10], Instruction[11], Instruction[12], Instruction[13], Instruction[14], Instruction[15]};
  assign OPCODE = Instruction[3:0];

  // Other names for the same wires on the sheet: Input1[7:0] = {Instruction[8], Instruction[9], Instruction[10], Instruction[11], Instruction[12], Instruction[13], Instruction[14], Instruction[15]}
endmodule
